# Fritzing sketch SnakeRobot_V1 (saved by Fritzing 0.9.0b)

parts:
  J1 = Basic Servo
  J2 = Basic Servo
  J3 = Basic Servo
  J4 = Basic Servo
  U1 = LIPO-110mAh [package=lipo-110]
  U2 = LIPO-110mAh [package=lipo-110]
  J5 = Basic Servo
  J6 = Basic Servo
  J7 = Basic Servo
  Part1 = Arduino Pro Mini v13
  J8 = Basic Servo
  IC1 = Voltage Regulator [package=to-220-alt]
  IC2 = Voltage Regulator [package=to-220-alt]
  J9 = Basic Servo
  J10 = Basic Servo
  J11 = Basic Servo
  J12 = Basic Servo
  U3 = LIPO-110mAh [package=lipo-110]
  IC3 = Voltage Regulator [package=to-220-alt]

nets:
  N1: J1.pulse, Part1.D2
  N2: J2.pulse, Part1.D1/RX
  N3: J3.gnd, U1.-
  N4: J3.vcc, IC1.OUT
  N5: J3.pulse, Part1.D4
  N6: J4.pulse, Part1.D3_PWM
  N7: U1.+, IC1.IN
  N8: U2.+, IC2.IN
  N9: J5.pulse, Part1.D5_PWM
  N10: J6.pulse, Part1.D6_PWM
  N11: J7.pulse, Part1.D7
  N12: Part1.D13/SCK, J11.pulse
  N13: Part1.D12/MISO, J10.pulse
  N14: Part1.D10_PWM/SS, J9.pulse
  N15: Part1.D9_PWM, J12.pulse
  N16: Part1.D8, J8.pulse
  N17: J8.vcc, IC2.OUT
  GND: J11.gnd, U3.-, IC3.GND
  N18: J11.vcc, IC3.OUT
  N19: U3.+, IC3.IN

notes:
  PS2 Controller
  Clock 14
  Command 15
  Attention 11
  Data 16
